// Logisim project Exemplo_0505.circ as structural Verilog: 1 circuit, main circuit main
module main (
  input  in_1,
  input  in_2,
  output out_3
);

  wire nor_1_out, nor_2_out, nor_3_out, nor_4_out, nor_5_out;

  not nor_1 (nor_1_out, in_1);  // NOR_Gate
  not nor_2 (nor_2_out, in_2);  // NOR_Gate
  not nor_3 (nor_3_out, nor_1_out);  // NOR_Gate
  not nor_4 (nor_4_out, nor_2_out);  // NOR_Gate
  nor nor_5 (nor_5_out, nor_3_out, nor_4_out);
  not nor_6 (out_3, nor_5_out);  // NOR_Gate
endmodule
