// Logisim project Exemplo_0603.circ as structural Verilog: 2 circuits, main circuit main
module main (
  input  in_1,
  input  in_2,
  input  in_3,
  input  in_4,
  output out_5
);

  wire and_1_out, mux2_1_out_4, mux2_2_out_4, nand_1_out, nor_1_out, not_1_out, or_1_out;

  nor nor_1 (nor_1_out, in_2, in_1);
  nand nand_1 (nand_1_out, in_2, in_1);
  and and_1 (and_1_out, in_2, in_1);
  or or_1 (or_1_out, in_2, in_1);
  Mux2 mux2_1 (.A(and_1_out), .B(or_1_out), .select(in_3), .out_4(mux2_1_out_4));
  Mux2 mux2_2 (.A(nor_1_out), .B(nand_1_out), .select(not_1_out), .out_4(mux2_2_out_4));
  not not_1 (not_1_out, in_3);
  Mux2 mux2_3 (.A(mux2_1_out_4), .B(mux2_2_out_4), .select(in_4), .out_4(out_5));
endmodule

module Mux2 (
  input  A,
  input  B,
  input  select,
  output out_4
);

  wire and_1_out, and_2_out, not_1_out;

  not not_1 (not_1_out, select);
  and and_1 (and_1_out, A, not_1_out);
  and and_2 (and_2_out, B, select);
  or or_1 (out_4, and_1_out, and_2_out);
endmodule
