// Logisim project Exemplo_0604.circ as structural Verilog: 2 circuits, main circuit main
module main (
  input  in_1,
  input  in_2,
  input  in_3,
  input  in_4,
  output out_5
);

  wire mux2_1_out_4, mux2_2_out_4, nor_1_out, not_1_out, or_1_out, xnor_1_out, xor_1_out;

  or or_1 (or_1_out, in_2, in_1);
  nor nor_1 (nor_1_out, in_2, in_1);
  xor xor_1 (xor_1_out, in_2, in_1);
  xnor xnor_1 (xnor_1_out, in_2, in_1);
  not not_1 (not_1_out, in_4);
  Mux2 mux2_1 (.A(or_1_out), .B(nor_1_out), .select(in_4), .out_4(mux2_1_out_4));
  Mux2 mux2_2 (.A(xor_1_out), .B(xnor_1_out), .select(not_1_out), .out_4(mux2_2_out_4));
  Mux2 mux2_3 (.A(mux2_1_out_4), .B(mux2_2_out_4), .select(in_3), .out_4(out_5));
endmodule

module Mux2 (
  input  A,
  input  B,
  input  select,
  output out_4
);

  wire and_1_out, and_2_out, not_1_out;

  not not_1 (not_1_out, select);
  and and_1 (and_1_out, A, not_1_out);
  and and_2 (and_2_out, B, select);
  or or_1 (out_4, and_1_out, and_2_out);
endmodule
