// Logisim project Exemplo_0605.circ as structural Verilog: 2 circuits, main circuit main
module main (
  input  in_1,
  input  in_2,
  input  in_3,
  input  in_4,
  input  in_5,
  output out_6
);

  wire and_1_out, mux2_1_out_4, mux2_2_out_4, mux2_3_out_4, mux2_4_out_4, mux2_5_out_4, mux2_6_out_4,
       nand_1_out, nor_1_out, not_1_out, not_3_out, not_4_out, not_5_out, or_1_out, xnor_1_out, xor_1_out;

  not not_1 (not_1_out, in_1);
  not not_2 (not_1_out, in_1);
  and and_1 (and_1_out, in_1, in_1);
  nand nand_1 (nand_1_out, in_1, in_1);
  nor nor_1 (nor_1_out, in_1, in_1);
  or or_1 (or_1_out, in_1, in_1);
  xor xor_1 (xor_1_out, in_1, in_1);
  xnor xnor_1 (xnor_1_out, in_1, in_1);
  not not_3 (not_3_out, in_5);
  not not_4 (not_4_out, in_5);
  Mux2 mux2_1 (.A(not_1_out), .B(not_1_out), .select(in_5), .out_4(mux2_1_out_4));
  Mux2 mux2_2 (.A(and_1_out), .B(nand_1_out), .select(not_3_out), .out_4(mux2_2_out_4));
  Mux2 mux2_3 (.A(nor_1_out), .B(or_1_out), .select(in_5), .out_4(mux2_3_out_4));
  Mux2 mux2_4 (.A(xor_1_out), .B(xnor_1_out), .select(not_4_out), .out_4(mux2_4_out_4));
  Mux2 mux2_5 (.A(mux2_1_out_4), .B(mux2_2_out_4), .select(in_4), .out_4(mux2_5_out_4));
  Mux2 mux2_6 (.A(mux2_3_out_4), .B(mux2_4_out_4), .select(not_5_out), .out_4(mux2_6_out_4));
  not not_5 (not_5_out, in_4);
  Mux2 mux2_7 (.A(mux2_5_out_4), .B(mux2_6_out_4), .select(in_3), .out_4(out_6));

  assign in_2 = in_1;
endmodule

module Mux2 (
  input  A,
  input  B,
  input  select,
  output out_4
);

  wire and_1_out, and_2_out, not_1_out;

  not not_1 (not_1_out, select);
  and and_1 (and_1_out, A, not_1_out);
  and and_2 (and_2_out, B, select);
  or or_1 (out_4, and_1_out, and_2_out);
endmodule
