// Logisim project Exemplo_0805.circ as structural Verilog: 1 circuit, main circuit main
module main (
  input  in_1,
  input  in_2,
  input  in_3,
  input  in_4,
  input  in_5,
  output out_6,
  output out_7,
  output out_8
);

  wire and_1_out, and_2_out, and_3_out, and_4_out, and_5_out, and_6_out, and_7_out, and_8_out, and_9_out,
       and_10_out, and_11_out, and_12_out, not_1_out, not_2_out, not_3_out, not_4_out, not_5_out, not_6_out,
       not_7_out, not_8_out, not_9_out, not_10_out, not_11_out, not_12_out, or_1_out, or_3_out, or_4_out;

  not not_1 (not_1_out, in_3);
  not not_2 (not_2_out, not_1_out);
  not not_3 (not_3_out, in_5);
  and and_1 (and_1_out, not_2_out, in_5);
  and and_2 (and_2_out, not_3_out, not_1_out);
  or or_1 (or_1_out, and_1_out, and_2_out);
  and and_3 (and_3_out, not_1_out, in_5);
  not not_4 (not_4_out, in_1);
  and and_4 (and_4_out, not_4_out, not_5_out);
  not not_5 (not_5_out, or_1_out);
  not not_6 (not_6_out, not_4_out);
  and and_5 (and_5_out, not_6_out, or_1_out);
  and and_6 (and_6_out, or_1_out, not_4_out);
  or or_2 (out_6, and_4_out, and_5_out);
  or or_3 (or_3_out, and_6_out, and_3_out);
  not not_7 (not_7_out, in_2);
  not not_8 (not_8_out, or_3_out);
  not not_9 (not_9_out, not_7_out);
  and and_7 (and_7_out, not_9_out, or_3_out);
  and and_8 (and_8_out, not_7_out, not_8_out);
  and and_9 (and_9_out, or_3_out, not_7_out);
  or or_4 (or_4_out, and_7_out, and_8_out);
  not not_10 (not_10_out, in_4);
  not not_11 (not_11_out, not_10_out);
  not not_12 (not_12_out, or_4_out);
  and and_10 (and_10_out, not_11_out, or_4_out);
  and and_11 (and_11_out, not_12_out, not_10_out);
  and and_12 (and_12_out, or_4_out, not_10_out);
  or or_5 (out_7, and_10_out, and_11_out);
  or or_6 (out_8, and_12_out, and_9_out);
endmodule
