// Logisim project Ex1.circ as structural Verilog: 3 circuits, main circuit 1X1
module _1X1 (
  input  Add,
  input  R_W,
  input  Clk,
  input  in_4,
  input  in,
  output out_6
);

  wire and_1_out, j_k_ff_1_q, not_1_out;

  and and_1 (and_1_out, Add, R_W, Clk);
  J_K_Flip_Flop j_k_ff_1 (
    .J(in), .clk(and_1_out), .K(not_1_out), .Q(j_k_ff_1_q), .reset(in_4));  // open: Qn, preset, en
  not not_1 (not_1_out, in);
  and and_2 (out_6, Add, j_k_ff_1_q);
endmodule

module _1X2 (
  input  Add,
  input  R_W,
  input  Clk,
  input  in0,
  input  in1,
  input  Clr,
  output out1,
  output out0
);

  _1X1 u_1x1_1 (.Add(Add), .R_W(R_W), .Clk(Clk), .in(in0), .in_4(Clr), .out_6(out0));
  _1X1 u_1x1_2 (.Add(Add), .R_W(R_W), .Clk(Clk), .in(in1), .in_4(Clr), .out_6(out1));
endmodule

module main (
  input  Add,
  input  R_W,
  input  Clk,
  input  in0,
  input  in1,
  input  Clr,
  input  in2,
  input  in3,
  output out3,
  output out2,
  output out1,
  output out0
);

  _1X2 u_1x2_1 (.Add(Add), .R_W(R_W), .Clk(Clk), .in0(in0), .in1(in1), .Clr(Clr), .out1(out1), .out0(out0));
  _1X2 u_1x2_2 (.Add(Add), .R_W(R_W), .Clk(Clk), .in0(in2), .in1(in3), .Clr(Clr), .out1(out3), .out0(out2));
endmodule
