// Logisim project Ex3.circ as structural Verilog: 1 circuit, main circuit main
module main (
  input  Add,
  input  R_W,
  input  Clk,
  input  in_4,
  input  in_5,
  input  in0,
  input  in_7,
  input  in_8,
  input  in1,
  input  in_10,
  input  in_11,
  input  in2,
  input  in3,
  output out_14,
  output out_15,
  output out_16,
  output out_17,
  output out_18,
  output out_19,
  output out_20,
  output out_21
);

  Ex1_main main_1 (
    .Add(Add), .R_W(R_W), .Clk(Clk), .in0(in0), .in1(in1), .in2(in2), .in3(in3), .out0(out_17), .Clr(in_7),
    .out3(out_21), .out2(out_20), .out1(out_19));
  Ex1_main main_2 (
    .Add(Add), .R_W(R_W), .Clk(Clk), .in0(in_4), .in1(in_5), .in2(in_8), .in3(in_11), .out0(out_18),
    .Clr(in_10), .out3(out_14), .out2(out_15), .out1(out_16));
endmodule
