// Logisim project Exercício4.circ as structural Verilog: 1 circuit, main circuit main
module main (
  input  in_1,
  input  in_2,
  output out_3,
  output out_4,
  output out_5,
  output out_6,
  output out_7
);

  wire clock_1_out, d_ff_5_q, or_1_out;

  Clock clock_1 (.out(clock_1_out));
  D_Flip_Flop d_ff_1 (.clk(clock_1_out), .D(out_4), .Q(out_3), .reset(in_2));  // open: Qn, preset, en
  or or_1 (or_1_out, out_3, in_1);
  D_Flip_Flop d_ff_2 (.clk(clock_1_out), .D(out_5), .Q(out_4), .reset(in_2));  // open: Qn, preset, en
  D_Flip_Flop d_ff_3 (.clk(clock_1_out), .D(out_6), .Q(out_5), .reset(in_2));  // open: Qn, preset, en
  D_Flip_Flop d_ff_4 (.clk(clock_1_out), .D(d_ff_5_q), .Q(out_6), .reset(in_2));  // open: Qn, preset, en
  not not_1 (out_7, d_ff_5_q);
  D_Flip_Flop d_ff_5 (.clk(clock_1_out), .D(or_1_out), .Q(d_ff_5_q), .reset(in_2));  // open: Qn, preset, en
endmodule
