// Logisim project Ex01.circ as structural Verilog: 1 circuit, main circuit main
module main (
  input  Pulse,
  input  CLR,
  output out_3,
  output out_4,
  output out_5,
  output out_6,
  output out_7
);

  J_K_Flip_Flop j_k_ff_1 (.J(1'b1), .clk(out_4), .K(1'b1), .Qn(out_3), .reset(CLR));  // open: Q, preset, en
  J_K_Flip_Flop j_k_ff_2 (.J(1'b1), .clk(out_5), .K(1'b1), .Qn(out_4), .reset(CLR));  // open: Q, preset, en
  J_K_Flip_Flop j_k_ff_3 (.J(1'b1), .clk(out_6), .K(1'b1), .Qn(out_5), .reset(CLR));  // open: Q, preset, en
  J_K_Flip_Flop j_k_ff_4 (.J(1'b1), .clk(out_7), .K(1'b1), .Qn(out_6), .reset(CLR));  // open: Q, preset, en
  J_K_Flip_Flop j_k_ff_5 (.J(1'b1), .clk(Pulse), .K(1'b1), .Qn(out_7), .reset(CLR));  // open: Q, preset, en
endmodule
