// Logisim project Ex03.circ as structural Verilog: 1 circuit, main circuit main
module main (
  input  Pulse,
  input  CLR,
  output out_3,
  output out_4,
  output out_5,
  output out_6,
  output out_7
);

  wire and_1_out, j_k_ff_2_qn, j_k_ff_3_qn, j_k_ff_4_qn, j_k_ff_5_qn, not_1_out, not_2_out, not_3_out,
       or_1_out;

  J_K_Flip_Flop j_k_ff_1 (.J(1'b1), .clk(j_k_ff_2_qn), .K(1'b1), .Q(out_3), .reset(or_1_out));  // open: Qn, preset, en
  or or_1 (or_1_out, and_1_out, CLR);
  J_K_Flip_Flop j_k_ff_2 (
    .J(1'b1), .clk(j_k_ff_3_qn), .K(1'b1), .Q(out_4), .Qn(j_k_ff_2_qn), .reset(or_1_out));  // open: preset, en
  and and_1 (and_1_out, not_1_out, out_4, not_2_out, out_6, not_3_out);
  not not_1 (not_1_out, out_3);
  not not_2 (not_2_out, out_5);
  not not_3 (not_3_out, out_7);
  J_K_Flip_Flop j_k_ff_3 (
    .J(1'b1), .clk(j_k_ff_4_qn), .K(1'b1), .Q(out_5), .Qn(j_k_ff_3_qn), .reset(or_1_out));  // open: preset, en
  J_K_Flip_Flop j_k_ff_4 (
    .J(1'b1), .clk(j_k_ff_5_qn), .K(1'b1), .Q(out_6), .Qn(j_k_ff_4_qn), .reset(or_1_out));  // open: preset, en
  J_K_Flip_Flop j_k_ff_5 (
    .J(1'b1), .clk(Pulse), .K(1'b1), .Q(out_7), .Qn(j_k_ff_5_qn), .reset(or_1_out));  // open: preset, en
endmodule
