// Logisim project Ex04.circ as structural Verilog: 1 circuit, main circuit main
module main (
  input  Pulse,
  input  CLR,
  output out_3,
  output out_4,
  output out_5,
  output out_6,
  output out_7
);

  wire and_1_out, not_1_out, not_2_out, or_1_out;

  J_K_Flip_Flop j_k_ff_1 (.J(1'b1), .clk(out_4), .K(1'b1), .Qn(out_3), .reset(or_1_out));  // open: Q, preset, en
  or or_1 (or_1_out, CLR, and_1_out);
  not not_1 (not_1_out, out_4);
  J_K_Flip_Flop j_k_ff_2 (.J(1'b1), .clk(out_5), .K(1'b1), .Qn(out_4), .reset(or_1_out));  // open: Q, preset, en
  and and_1 (and_1_out, out_3, not_1_out, out_5, not_2_out, out_7);
  not not_2 (not_2_out, out_6);
  J_K_Flip_Flop j_k_ff_3 (.J(1'b1), .clk(out_6), .K(1'b1), .Qn(out_5), .reset(or_1_out));  // open: Q, preset, en
  J_K_Flip_Flop j_k_ff_4 (.J(1'b1), .clk(out_7), .K(1'b1), .Qn(out_6), .reset(or_1_out));  // open: Q, preset, en
  J_K_Flip_Flop j_k_ff_5 (.J(1'b1), .clk(Pulse), .K(1'b1), .Qn(out_7), .reset(or_1_out));  // open: Q, preset, en
endmodule
