// Logisim project Ex05.circ as structural Verilog: 1 circuit, main circuit main
module main (
  input  Pulse,
  input  CLR,
  output out_3,
  output out_4,
  output out_5,
  output out_6,
  output out_7
);

  wire and_1_out, not_1_out, not_2_out, not_3_out, or_1_out, t_ff_2_qn, t_ff_3_qn, t_ff_4_qn, t_ff_5_qn;

  T_Flip_Flop t_ff_1 (.clk(t_ff_2_qn), .T(t_ff_2_qn), .Q(out_3), .reset(or_1_out));  // open: Qn, preset, en
  or or_1 (or_1_out, CLR, and_1_out);
  T_Flip_Flop t_ff_2 (.clk(t_ff_3_qn), .T(t_ff_3_qn), .Q(out_4), .Qn(t_ff_2_qn), .reset(or_1_out));  // open: preset, en
  and and_1 (and_1_out, not_2_out, out_4, not_1_out, out_6, not_3_out);
  not not_1 (not_1_out, out_5);
  not not_2 (not_2_out, out_3);
  T_Flip_Flop t_ff_3 (.clk(t_ff_4_qn), .T(t_ff_4_qn), .Q(out_5), .Qn(t_ff_3_qn), .reset(or_1_out));  // open: preset, en
  not not_3 (not_3_out, out_7);
  T_Flip_Flop t_ff_4 (.clk(t_ff_5_qn), .T(t_ff_5_qn), .Q(out_6), .Qn(t_ff_4_qn), .reset(or_1_out));  // open: preset, en
  T_Flip_Flop t_ff_5 (.clk(Pulse), .T(Pulse), .Q(out_7), .Qn(t_ff_5_qn), .reset(or_1_out));  // open: preset, en
endmodule
