// Logisim project Ex06.circ as structural Verilog: 1 circuit, main circuit main
module main (
  input  Set,
  input  CLR,
  output out_3,
  output out_4,
  output out_5,
  output out_6,
  output out_7
);

  wire CLK_out, j_k_ff_1_qn, j_k_ff_2_qn, j_k_ff_3_qn, j_k_ff_4_qn, j_k_ff_5_qn;

  Clock CLK (.out(CLK_out));
  J_K_Flip_Flop j_k_ff_1 (
    .J(out_7), .clk(CLK_out), .K(j_k_ff_5_qn), .Q(out_3), .Qn(j_k_ff_1_qn), .preset(Set), .reset(CLR));  // open: en
  J_K_Flip_Flop j_k_ff_2 (
    .J(out_3), .clk(CLK_out), .K(j_k_ff_1_qn), .Q(out_4), .Qn(j_k_ff_2_qn), .reset(CLR));  // open: preset, en
  J_K_Flip_Flop j_k_ff_3 (
    .J(out_4), .clk(CLK_out), .K(j_k_ff_2_qn), .Q(out_5), .Qn(j_k_ff_3_qn), .reset(CLR));  // open: preset, en
  J_K_Flip_Flop j_k_ff_4 (
    .J(out_5), .clk(CLK_out), .K(j_k_ff_3_qn), .Q(out_6), .Qn(j_k_ff_4_qn), .reset(CLR));  // open: preset, en
  J_K_Flip_Flop j_k_ff_5 (
    .J(out_6), .clk(CLK_out), .K(j_k_ff_4_qn), .Q(out_7), .Qn(j_k_ff_5_qn), .reset(CLR));  // open: preset, en
endmodule
