// Logisim project Somatorio.circ as structural Verilog: 1 circuit, main circuit main
module main (
  input  A,
  input  B,
  input  A_2,
  input  B_2,
  input  in_5,
  output out_6,
  output out_7,
  output out_8
);

  wire and_1_out, and_2_out, and_3_out, and_4_out, and_5_out, and_6_out, and_7_out, and_8_out, and_9_out,
       and_10_out, and_11_out, and_12_out, or_1_out, or_3_out, or_4_out;

  and and_1 (and_1_out, ~in_5, A);  // AND_Gate
  and and_2 (and_2_out, in_5, ~A);  // AND_Gate
  and and_3 (and_3_out, in_5, A);
  or or_1 (or_1_out, and_1_out, and_2_out);
  and and_4 (and_4_out, ~or_1_out, B);  // AND_Gate
  and and_5 (and_5_out, or_1_out, ~B);  // AND_Gate
  and and_6 (and_6_out, or_1_out, B);
  or or_2 (out_6, and_4_out, and_5_out);
  or or_3 (or_3_out, and_6_out, and_3_out);
  and and_7 (and_7_out, ~or_3_out, A_2);  // AND_Gate
  or or_4 (or_4_out, and_7_out, and_8_out);
  and and_8 (and_8_out, or_3_out, ~A_2);  // AND_Gate
  and and_9 (and_9_out, or_3_out, A_2);
  and and_10 (and_10_out, ~or_4_out, B_2);  // AND_Gate
  and and_11 (and_11_out, or_4_out, ~B_2);  // AND_Gate
  and and_12 (and_12_out, or_4_out, B_2);
  or or_5 (out_7, and_10_out, and_11_out);
  or or_6 (out_8, and_12_out, and_9_out);
endmodule
