// Logisim project AAA.circ as structural Verilog: 3 circuits, main circuit main
module main (
  input  A0,
  input  B0,
  input  A1,
  input  B1,
  input  A2,
  input  B2,
  input  A3,
  input  B3,
  input  in_9,
  output _128,
  output _64,
  output _32,
  output _16,
  output _8,
  output _4,
  output _2,
  output _1
);

  Multiplicando multiplicando_1 (
    .A0(A0), .B0(B0), .A1(A1), .B1(B1), .A2(A2), .B2(B2), .A3(A3), .B3(B3), ._128(_128), ._64(_64),
    ._32(_32), ._16(_16), ._8(_8), ._4(_4), ._2(_2), ._1(_1), .in_9(in_9));
endmodule

module Somador (
  input  CarryIn,
  input  A,
  input  B,
  output Soma,
  output CarryOut
);

  wire and_1_out, and_2_out, xor_1_out;

  xor xor_1 (xor_1_out, A, B);
  and and_1 (and_1_out, A, B);
  xor xor_2 (Soma, CarryIn, xor_1_out);
  and and_2 (and_2_out, CarryIn, xor_1_out);
  or or_1 (CarryOut, and_2_out, and_1_out);
endmodule

module Multiplicando (
  input  A0,
  input  B0,
  input  A1,
  input  B1,
  input  A2,
  input  B2,
  input  A3,
  input  B3,
  input  in_9,
  output _128,
  output _64,
  output _4,
  output _2,
  output _1,
  output _32,
  output _16,
  output _8
);

  wire A0B1_out, A0B2_out, A0B3_out, A1B0_out, A1B1_out, A1B2_out, A1B3_out, A2B0_out, A2B1_out, A2B2_out,
       A2B3_out, A3B0_out, A3B1_out, A3B2_out, A3B3_out, somador_2_carryout, somador_3_carryout,
       somador_3_soma, somador_4_carryout, somador_5_carryout, somador_5_soma, somador_6_carryout,
       somador_6_soma, somador_7_carryout, somador_7_soma, somador_8_carryout, somador_9_carryout,
       somador_9_soma, somador_10_carryout, somador_10_soma, somador_11_carryout, somador_12_carryout;

  Somador somador_1 (.CarryIn(somador_2_carryout), .A(somador_3_carryout), .B(A3B3_out), .Soma(_64), .CarryOut(_128));
  and A3B3 (A3B3_out, A3, B3);
  Somador somador_2 (.CarryIn(somador_3_soma), .A(A3B2_out), .B(A2B3_out), .Soma(_32), .CarryOut(somador_2_carryout));
  and A1B3 (A1B3_out, A1, B3);
  and A2B3 (A2B3_out, A2, B3);
  Somador somador_3 (
    .CarryIn(somador_5_carryout), .A(somador_4_carryout), .B(somador_6_carryout), .Soma(somador_3_soma),
    .CarryOut(somador_3_carryout));
  and A0B3 (A0B3_out, A0, B3);
  Somador somador_4 (.CarryIn(in_9), .A(somador_5_soma), .B(A1B3_out), .Soma(_16), .CarryOut(somador_4_carryout));
  and A2B2 (A2B2_out, A2, B2);
  and A3B2 (A3B2_out, A3, B2);
  Somador somador_5 (
    .CarryIn(somador_6_soma), .A(A3B1_out), .B(A2B2_out), .Soma(somador_5_soma), .CarryOut(somador_5_carryout));
  and A1B2 (A1B2_out, A1, B2);
  Somador somador_6 (
    .CarryIn(somador_9_carryout), .A(somador_7_carryout), .B(somador_8_carryout), .Soma(somador_6_soma),
    .CarryOut(somador_6_carryout));
  and A3B1 (A3B1_out, A3, B1);
  and A0B2 (A0B2_out, A0, B2);
  and A2B1 (A2B1_out, A2, B1);
  Somador somador_7 (
    .CarryIn(somador_9_soma), .A(A2B1_out), .B(A1B2_out), .Soma(somador_7_soma), .CarryOut(somador_7_carryout));
  Somador somador_8 (.CarryIn(in_9), .A(A0B3_out), .B(somador_7_soma), .Soma(_8), .CarryOut(somador_8_carryout));
  and A0B1 (A0B1_out, A0, B1);
  and A1B1 (A1B1_out, A1, B1);
  Somador somador_9 (
    .CarryIn(somador_11_carryout), .A(somador_10_carryout), .B(A3B0_out), .Soma(somador_9_soma),
    .CarryOut(somador_9_carryout));
  and A3B0 (A3B0_out, A3, B0);
  and A2B0 (A2B0_out, A2, B0);
  Somador somador_10 (
    .CarryIn(somador_12_carryout), .A(A2B0_out), .B(A1B1_out), .Soma(somador_10_soma),
    .CarryOut(somador_10_carryout));
  Somador somador_11 (.CarryIn(in_9), .A(somador_10_soma), .B(A0B2_out), .Soma(_4), .CarryOut(somador_11_carryout));
  and A1B0 (A1B0_out, A1, B0);
  Somador somador_12 (.CarryIn(in_9), .A(A1B0_out), .B(A0B1_out), .Soma(_2), .CarryOut(somador_12_carryout));
  and A0B0 (_1, A0, B0);
endmodule
