// Logisim project Rel1.circ as structural Verilog: 3 circuits, main circuit main
module main (
  input  A0,
  input  B0,
  input  A1,
  input  B1,
  input  A2,
  input  B2,
  input  A3,
  input  B3,
  output S0,
  output S1,
  output S2,
  output S3,
  output Carry_out
);

  wire somador_completo_1_carry_out, somador_completo_2_carry_out, somador_completo_3_carry_out;

  Somador_completo somador_completo_1 (
    .A(A0), .B(B0), .Carry_in(1'b0), .Carry_out(somador_completo_1_carry_out), .S(S0));
  Somador_completo somador_completo_2 (
    .A(A1), .B(B1), .Carry_in(somador_completo_1_carry_out), .Carry_out(somador_completo_2_carry_out), .S(S1));
  Somador_completo somador_completo_3 (
    .A(A2), .B(B2), .Carry_in(somador_completo_2_carry_out), .Carry_out(somador_completo_3_carry_out), .S(S2));
  Somador_completo somador_completo_4 (
    .A(A3), .B(B3), .Carry_in(somador_completo_3_carry_out), .Carry_out(Carry_out), .S(S3));
endmodule

module Meio_somador (
  input  A,
  input  B,
  output Soma,
  output Vai_1
);

  xor xor_1 (Soma, A, B);
  and and_1 (Vai_1, A, B);
endmodule

module Somador_completo (
  input  Carry_in,
  input  A,
  input  B,
  output S,
  output Carry_out
);

  wire and_1_out, and_2_out, xor_1_out;

  xor xor_1 (xor_1_out, A, B);
  and and_1 (and_1_out, A, B);
  or or_1 (Carry_out, and_1_out, and_2_out);
  xor xor_2 (S, xor_1_out, Carry_in);
  and and_2 (and_2_out, xor_1_out, Carry_in);
endmodule
