// Logisim project ULA.circ as structural Verilog: 3 circuits, main circuit ULA1
// ULA
module ULA1 (
  input  carry_in,
  input  b_invert,
  input  a0,
  input  op1,
  input  op2,
  input  b0,
  output S0,
  output Carry_out
);

  wire adder_1_out, and_1_out, multiplexer_1_out, not_1_out, not_2_out, or_1_out;

  not not_1 (not_1_out, b0);
  Multiplexer #(.enable("false")) multiplexer_1 (.in0(b0), .in1(not_1_out), .out(multiplexer_1_out), .sel(b_invert));
  and and_1 (and_1_out, a0, multiplexer_1_out);
  or or_1 (or_1_out, a0, multiplexer_1_out);
  not not_2 (not_2_out, a0);
  Multiplexer #(.select(2), .enable("false")) multiplexer_2 (
    .in0(and_1_out), .in1(or_1_out), .in2(not_2_out), .in3(adder_1_out), .out(S0), .sel({op2, op1}));
  Adder #(.width(1)) adder_1 (.a(a0), .b(multiplexer_1_out), .out(adder_1_out), .cin(carry_in), .cout(Carry_out));
endmodule

module ULA2 (
  input  A0,
  input  A1,
  input  B0,
  input  B1,
  input  op1,
  input  op2,
  input  B_invert,
  output S0,
  output S1,
  output Carry_out
);

  wire ula1_1_carry_out;

  ULA1 ula1_1 (
    .a0(A0), .b0(B0), .b_invert(B_invert), .carry_in(B_invert), .Carry_out(ula1_1_carry_out), .S0(S0),
    .op1(op1), .op2(op2));
  ULA1 ula1_2 (
    .a0(A1), .b0(B1), .b_invert(B_invert), .carry_in(ula1_1_carry_out), .Carry_out(Carry_out), .S0(S1),
    .op1(op1), .op2(op2));
endmodule

module ULA4 (
  input  B3,
  input  A3,
  input  B2,
  input  A2,
  input  B1,
  input  A1,
  input  B0,
  input  A0,
  input  B_invert,
  input  Op1,
  input  Op2,
  output S1,
  output S0,
  output Carry_Out,
  output S3,
  output S2
);

  wire ula1_2_carry_out, ula1_3_carry_out, ula1_4_carry_out;

  ULA1 ula1_1 (
    .a0(A3), .b0(B3), .b_invert(B_invert), .carry_in(ula1_2_carry_out), .Carry_out(Carry_Out), .S0(S3),
    .op1(Op1), .op2(Op2));
  ULA1 ula1_2 (
    .a0(A2), .b0(B2), .b_invert(B_invert), .carry_in(ula1_3_carry_out), .Carry_out(ula1_2_carry_out),
    .S0(S2), .op1(Op1), .op2(Op2));
  ULA1 ula1_3 (
    .a0(A1), .b0(B1), .b_invert(B_invert), .carry_in(ula1_4_carry_out), .Carry_out(ula1_3_carry_out),
    .S0(S1), .op1(Op1), .op2(Op2));
  ULA1 ula1_4 (
    .a0(A0), .b0(B0), .b_invert(B_invert), .carry_in(B_invert), .Carry_out(ula1_4_carry_out), .S0(S0),
    .op1(Op1), .op2(Op2));
endmodule
